# Fritzing sketch ESPrinkler2 (saved by Fritzing 0.9.2b)
circuit board: 8.46667cm x 5.64444cm
breadboards: 1

parts:
  U1 = 74HC595 [package="DIP16 [THT]"]
  OLED1 = OLED 0.96" 128x64 I2C SSD1306
  Q1 = NPN-Transistor [part_number=2n2222 package="TO92 [THT]"]
  R1 = Resistor [tolerance=±5% resistance=10k package=THT]
  WeMos_D1_Mini1 = WeMos D1 Mini
  K1 = RELAY [package=relay-g5q]
  K2 = RELAY [package=relay-g5q]
  Q2 = NPN-Transistor [part_number=2n2222 package="TO92 [THT]"]
  R2 = Resistor [tolerance=±5% resistance=10k package=THT]

nets:
  N1: U1.Q1, R2.Pin_1
  GND: U1.GND, U1.OE, OLED1.GND, Q1.E, WeMos_D1_Mini1.G, Q2.E
  N2: U1.SH_CP, WeMos_D1_Mini1.D5
  N3: U1.ST_CP, WeMos_D1_Mini1.D8
  N4: U1.DS, WeMos_D1_Mini1.D7
  N5: U1.Q0, R1.Pin_1
  5V: U1.VCC, OLED1.VCC, Q1.C, WeMos_D1_Mini1.5V, K1.COIL2, K1.COIL1, K2.COIL2
  N6: OLED1.SCL, WeMos_D1_Mini1.D1
  N7: OLED1.SCA, WeMos_D1_Mini1.D2
  N8: Q1.B, R1.Pin_0
  24vac: K1.MAIN, K2.MAIN
  N9: K1.NO, K2.NO
  Output 1: K1.NC
  Output 2: K2.NC
  N10: K2.COIL1, Q2.C
  N11: Q2.B, R2.Pin_0

notes:
  K3-K8, Q1-Q8, R1-R8
  all the same connected to Q2-Q7
  Illistration Purposes Only.
  ESPrinkler2
  0.1
  This schematic is intended as a general guide. DIY assembly and soldering skills are required to complete this project.
